# Fritzing sketch handkontroll_full_schematic (saved by Fritzing 1.0.1rc)
breadboards: 1

parts:
  R1 = Resistor [tolerance=±5% power=0.25W resistance=220 package=THT]  # not connected
  LED1 = LED - 5mm [color="Red (633nm)" current=0.030A package="5 mm [THT]"]
  Part1 = Arduino Nano (Rev3.0)
  JP1 = Header 4 [package=jst-4-pth]
  C1 = Capacitor [package=cap-pth-small2]  # not connected
  SG1 = Buzzer 12mm [package=buzzer-12mm]  # not connected
  JP2 = Header 2 [package=jst-2-pth]
  S2 = Pushbutton [package=THT]
  U1 = SWITCH-SPST-2 [package=switch-spst-vertical]
  VCC1 = Battery block 9V
  JP3 = Header 2 [package=jst-2-pth]
  JP4 = Header 4 [package=jst-4-pth]
  U2 = POT [knob_status=50% power=0.5W package=pot_mammoth]
  F1 = Resettable Fuse PTC [package=ptc-1206]  # not connected
  JP5 = Header 4 [package=jst-4-pth]

nets:
  Led-: LED1.cathode, JP1.4
  Led+: LED1.anode, JP1.3
  GND: Part1.GND, VCC1.-, JP3.2, JP5.4
  ON/OFF2: Part1.VIN, JP2.2, U1.P
  5V: Part1.5V, JP5.3
  SCL I2C: Part1.A5, JP5.1
  SDA I2C: Part1.A4, JP5.2
  S1: JP1.1, S2.leg0
  S2: JP1.2, S2.leg1
  9V/ON/OFF1: JP2.1, U1.O, VCC1.+, JP3.1
  Pot+: JP4.1, U2.A
  Pot-: JP4.2, U2.E
  PotS: JP4.3, U2.S
