# Fritzing sketch handkontroll_full_schematic_all_components (saved by Fritzing 0.9.3b)
circuit board: 8.36385cm x 5.29741cm
breadboards: 1

parts:
  R1 = Resistor [tolerance=±5% power=0.25W resistance=10k package=THT]
  Arduino_USB = Arduino Nano (Rev3.0)
  C1 = Capacitor [package=cap-pth-small2]
  Speaker = Buzzer 12mm [package=buzzer-12mm]
  R2 = Resistor [tolerance=±5% power=0.25W resistance=10k package=THT]
  R3 = Resistor [tolerance=±5% power=0.25W resistance=680 package=THT]
  R4 = Resistor [tolerance=±5% power=0.25W resistance=680 package=THT]
  R5 = Resistor [tolerance=±5% power=0.25W resistance=220 package=THT]
  D1 = Rectifier Diode [part_number=1N4001 package="300 mil [THT]"]
  F1 = Resettable Fuse PTC [package=ptc]
  VCC- = Battery block 9V
  Potmeter = molex pin header, 4 pins [form=molex]
  Button2 = molex pin header, 4 pins [form=molex]
  Button1 = molex pin header, 4 pins [form=molex]
  LCD_I2C = molex pin header, 4 pins [form=molex]
  Outputs = molex pin header, 4 pins [form=molex]
  Switch = molex pin header, 2 pins [form=molex]
  U2 = SWITCH-SPST-2 [package=switch-spst-vertical]
  LED2 = LED - 5mm [color="Red (633nm)" current=0.030A package="5 mm [THT]"]
  S3 = Pushbutton [package=THT]
  U3 = POT [knob_status=50% power=0.5W package=pot_mammoth]
  LED3 = LED - 5mm [color="Red (633nm)" current=0.030A package="5 mm [THT]"]
  S6 = Pushbutton [package=THT]

nets:
  S-_2: R1.Pin_0, Arduino_USB.D4, Button2.pin2, S6.leg1
  GND/Pot-: R1.Pin_1, Arduino_USB.GND, C1.2, Speaker.2, R2.Pin_1, R3.Pin_0, R4.Pin_0, VCC-.-, Potmeter.pin3, LCD_I2C.pin4, Outputs.pin4, U3.E
  S-_1: Arduino_USB.D2, R2.Pin_0, Button1.pin2, S3.leg1
  Led+_1: Arduino_USB.D3, Button1.pin3, LED2.anode
  Led+_2: Arduino_USB.D5, Button2.pin3, LED3.anode
  N1: Arduino_USB.D10, R5.Pin_0
  Out3: Arduino_USB.D11/MOSI, Outputs.pin3
  Out2: Arduino_USB.D12/MISO, Outputs.pin2
  ON/OFF2: Arduino_USB.VIN, Switch.pin2
  5V/Pot+/S+_1/S+_2: Arduino_USB.5V, Potmeter.pin1, Button2.pin1, Button1.pin1, LCD_I2C.pin3, U3.A
  SCL I2C: Arduino_USB.A5, LCD_I2C.pin1
  SDA I2C: Arduino_USB.A4, LCD_I2C.pin2
  PotS: Arduino_USB.A0, C1.1, Potmeter.pin2, U3.S
  Out1: Arduino_USB.D13/SCK, Outputs.pin1
  N2: Speaker.1, R5.Pin_1
  Led-_1: R3.Pin_1, Button1.pin4, LED2.cathode
  Led-_2: R4.Pin_1, Button2.pin4, LED3.cathode
  N3: D1.cathode, F1.1
  N4: D1.anode, VCC-.+
  ON/OFF1: F1.2, Switch.pin1, U2.O

notes:
  +
  Handkontroll v1.2
  github.com/robotikklinja/handkontroll
  -
