# Fritzing sketch handkontroll_full_schematic_pcb_4_buttons_auto_test (saved by Fritzing 1.0.2b)
circuit board: 7.83089cm x 5.05388cm
breadboards: 1

parts:
  Arduino_USB = Arduino Nano (Rev3.0)
  C1 = Capacitor [package=cap-pth-small2]
  Speaker = Buzzer 12mm [package=buzzer-12mm]
  R2 = Resistor [tolerance=±5% power=0.25W resistance=10k package=THT]
  R1 = Resistor [tolerance=±5% power=0.25W resistance=680 package=THT]
  R9 = Resistor [tolerance=±5% power=0.25W resistance=220 package=THT]
  D1 = Rectifier Diode [part_number=1N4001 package="300 mil [THT]"]
  F1 = Resettable Fuse PTC [package=ptc]
  Potmeter = molex pin header, 4 pins [form=molex]
  Button2 = molex pin header, 4 pins [form=molex]
  Button1 = molex pin header, 4 pins [form=molex]
  LCD_I2C = molex pin header, 4 pins [form=molex]
  Outputs = molex pin header, 4 pins [form=molex]
  R5 = Resistor [tolerance=±5% power=0.25W resistance=680 package=THT]
  R6 = Resistor [tolerance=±5% power=0.25W resistance=10k package=THT]
  Button3 = molex pin header, 4 pins [form=molex]
  R7 = Resistor [tolerance=±5% power=0.25W resistance=680 package=THT]
  R8 = Resistor [tolerance=±5% power=0.25W resistance=10k package=THT]
  Button4 = molex pin header, 4 pins [form=molex]
  R3 = Resistor [tolerance=±5% power=0.25W resistance=680 package=THT]
  R4 = Resistor [tolerance=±5% power=0.25W resistance=10k package=THT]
  Power = molex pin header, 4 pins [form=molex]

nets:
  S-_1: Arduino_USB.D2, R2.Pin_0, Button1.pin2
  Led+_1: Arduino_USB.D3, Button1.pin3
  S-_2: Arduino_USB.D4, Button2.pin2, R4.Pin_0
  Led+_2: Arduino_USB.D5, Button2.pin3
  Led+_3: Arduino_USB.D6, Button3.pin3
  S-_3: Arduino_USB.D7, R6.Pin_0, Button3.pin2
  S-_4: Arduino_USB.D8, R8.Pin_0, Button4.pin2
  Led+_4: Arduino_USB.D9, Button4.pin3
  Out1: Arduino_USB.D10, Outputs.pin1
  Out2: Arduino_USB.D11/MOSI, Outputs.pin2
  Out3: Arduino_USB.D12/MISO, Outputs.pin3
  ON/OFF-: Arduino_USB.VIN, Power.pin4
  GND/Pot-: Arduino_USB.GND, C1.2, Speaker.2, R2.Pin_1, R1.Pin_0, Potmeter.pin3, LCD_I2C.pin4, Outputs.pin4, R5.Pin_0, R6.Pin_1, R7.Pin_0, R8.Pin_1, R3.Pin_1, R4.Pin_1, Power.pin1
  5V/Pot+/S+_1/S+_2/S+_3/S+_4: Arduino_USB.5V, Potmeter.pin1, Button2.pin1, Button1.pin1, LCD_I2C.pin3, Button3.pin1, Button4.pin1
  SCL I2C: Arduino_USB.A5, LCD_I2C.pin1
  SDA I2C: Arduino_USB.A4, LCD_I2C.pin2
  PotS: Arduino_USB.A0, C1.1, Potmeter.pin2
  N1: Arduino_USB.D13/SCK, R9.Pin_0
  N2: Speaker.1, R9.Pin_1
  Led-_1: R1.Pin_1, Button1.pin4
  N3: D1.cathode, F1.1
  PowerIN: D1.anode, Power.pin2
  ON/OFF+: F1.2, Power.pin3
  Led-_2: Button2.pin4, R3.Pin_0
  Led-_3: R5.Pin_1, Button3.pin4
  Led-_4: R7.Pin_1, Button4.pin4

notes:
  Handkontroll v1.6
  github.com/robotikklinja/handkontroll
  +
  -
  To get the PWM on all LEDs
