# Fritzing sketch handkontroll_full_schematic_pcb_auto (saved by Fritzing 1.0.1rc)
circuit board: 8.36385cm x 5.29741cm
breadboards: 1

parts:
  R1 = Resistor [tolerance=±5% power=0.25W resistance=10k package=THT]
  Arduino_USB = Arduino Nano (Rev3.0)
  C1 = Capacitor [package=cap-pth-small2]
  Speaker = Buzzer 12mm [package=buzzer-12mm]
  R2 = Resistor [tolerance=±5% power=0.25W resistance=10k package=THT]
  R3 = Resistor [tolerance=±5% power=0.25W resistance=680 package=THT]
  R4 = Resistor [tolerance=±5% power=0.25W resistance=680 package=THT]
  R5 = Resistor [tolerance=±5% power=0.25W resistance=220 package=THT]
  D1 = Rectifier Diode [part_number=1N4001 package="300 mil [THT]"]
  F1 = Resettable Fuse PTC [package=ptc]
  VCC- = Battery block 9V
  Potmeter = molex pin header, 4 pins [form=molex]
  Button2 = molex pin header, 4 pins [form=molex]
  Button1 = molex pin header, 4 pins [form=molex]
  LCD_I2C = molex pin header, 4 pins [form=molex]
  Outputs = molex pin header, 4 pins [form=molex]
  Switch = molex pin header, 2 pins [form=molex]

nets:
  S2_2: R1.Pin_0, Arduino_USB.D4, Button2.pin2
  GND/Pot-: R1.Pin_1, Arduino_USB.GND, C1.2, Speaker.2, R2.Pin_1, R3.Pin_0, R4.Pin_0, VCC-.-, Potmeter.pin3, LCD_I2C.pin4, Outputs.pin4
  S2_1: Arduino_USB.D2, R2.Pin_0, Button1.pin2
  Led+_1: Arduino_USB.D3, Button1.pin3
  Led+_2: Arduino_USB.D5, Button2.pin3
  N1: Arduino_USB.D10, R5.Pin_0
  Out3: Arduino_USB.D11/MOSI, Outputs.pin3
  Out2: Arduino_USB.D12/MISO, Outputs.pin2
  ON/OFF2: Arduino_USB.VIN, Switch.pin2
  5V/Pot+/S1_1/S1_2: Arduino_USB.5V, Potmeter.pin1, Button2.pin1, Button1.pin1, LCD_I2C.pin3
  SCL I2C: Arduino_USB.A5, LCD_I2C.pin1
  SDA I2C: Arduino_USB.A4, LCD_I2C.pin2
  PotS: Arduino_USB.A0, C1.1, Potmeter.pin2
  Out1: Arduino_USB.D13/SCK, Outputs.pin1
  N2: Speaker.1, R5.Pin_1
  Led-_1: R3.Pin_1, Button1.pin4
  Led-_2: R4.Pin_1, Button2.pin4
  N3: D1.cathode, F1.1
  N4: D1.anode, VCC-.+
  ON/OFF1: F1.2, Switch.pin1

notes:
  +
  Handkontroll v1.2
  github.com/robotikklinja/handkontroll
  -
