# Fritzing sketch handkontroll_full_schematic_pcb_small_JSTs (saved by Fritzing 1.0.1rc)
circuit board: 8.36385cm x 5.29741cm
breadboards: 1

parts:
  R1 = Resistor [tolerance=±5% power=0.25W resistance=10k package=THT]
  Arduino_USB = Arduino Nano (Rev3.0)
  C1 = Capacitor [package=cap-pth-small2]
  Speaker = Buzzer 12mm [package=buzzer-12mm]
  Switch = Header 2 [package=jst-2-pth]
  Potmeter = Header 4 [package=jst-4-pth]
  LCD_I2C = Header 4 [package=jst-4-pth]
  Button1 = Header 4 [package=jst-4-pth]
  Button2 = Header 4 [package=jst-4-pth]
  R2 = Resistor [tolerance=±5% power=0.25W resistance=10k package=THT]
  R3 = Resistor [tolerance=±5% power=0.25W resistance=680 package=THT]
  R4 = Resistor [tolerance=±5% power=0.25W resistance=680 package=THT]
  Outputs = Header 4 [package=jst-4-pth]
  R5 = Resistor [tolerance=±5% power=0.25W resistance=220 package=THT]
  D1 = Rectifier Diode [part_number=1N4001 package="300 mil [THT]"]
  Fuse = Resettable Fuse PTC [package=ptc]
  VCC- = Battery block 9V

nets:
  S2_2: R1.Pin_0, Arduino_USB.D4, Button2.2
  GND/Pot-: R1.Pin_1, Arduino_USB.GND, C1.2, Speaker.2, Potmeter.3, LCD_I2C.4, R2.Pin_1, R3.Pin_0, R4.Pin_0, Outputs.4, VCC-.-
  S2_1: Arduino_USB.D2, Button1.2, R2.Pin_0
  Led+_1: Arduino_USB.D3, Button1.3
  Led+_2: Arduino_USB.D5, Button2.3
  N1: Arduino_USB.D10, R5.Pin_0
  Out3: Arduino_USB.D11/MOSI, Outputs.3
  Out2: Arduino_USB.D12/MISO, Outputs.2
  ON/OFF2: Arduino_USB.VIN, Switch.2
  5V/Pot+/S1_1/S1_2: Arduino_USB.5V, Potmeter.1, LCD_I2C.3, Button1.1, Button2.1
  SCL I2C: Arduino_USB.A5, LCD_I2C.1
  SDA I2C: Arduino_USB.A4, LCD_I2C.2
  PotS: Arduino_USB.A0, C1.1, Potmeter.2
  Out1: Arduino_USB.D13/SCK, Outputs.1
  N2: Speaker.1, R5.Pin_1
  ON/OFF1: Switch.1, Fuse.2
  Led-_1: Button1.4, R3.Pin_1
  Led-_2: Button2.4, R4.Pin_1
  N3: D1.cathode, Fuse.1
  N4: D1.anode, VCC-.+

notes:
  +
  Handkontroll v1.1
  github.com/robotikklinja/handkontroll
